// Logisim project K68-CPUB-DECODE.circ as structural Verilog: 1 circuit, main circuit main
module main (
  input  A15,
  input  A000,
  input  VMA,
  output RAMCE
);

  wire nand_1_out;

  nand nand_1 (nand_1_out, A15, A000);
  nand nand_2 (RAMCE, VMA, nand_1_out);
endmodule
